# Fritzing sketch hardwareConnections (saved by Fritzing 0.9.3b)
breadboards: 1

parts:
  Part1 = Arduino Nano (Rev3.0)
  R1 = Photocell (LDR) [package=THT]
  RHT1 = Humidity and Temperature Sensor RHT03
  R2 = Resistor [tolerance=±5% resistance=10k package=THT]

nets:
  N1: Part1.GND, RHT1.GND_2, R2.Pin_0
  5V: Part1.5V, R1.pin_1, RHT1.Vcc
  N2: Part1.A6, R1.pin_0, R2.Pin_1
  N3: Part1.A5, RHT1.Data-signal
